# Fritzing sketch esp8266_pzem017 (saved by Fritzing 0.9.10b)
circuit board: 5cm x 3.7cm
breadboards: 1

parts:
  WeMos_D1_Mini1 = WeMos D1 Mini
  U1 = MAX485 [part_number=MAX3485 package=dil08]
  R1 = Resistor [tolerance=±5% resistance=120 power=0.25 package=THT]
  J1 = screw terminal, 4 pins
  J2 = Screw terminal - 2 pins [package=THT]

nets:
  3V3: WeMos_D1_Mini1.3V3, U1.VCC
  N1: WeMos_D1_Mini1.5V, J1.pin1, J2.pin2
  N2: WeMos_D1_Mini1.D6, U1.RE, U1.DE
  N3: WeMos_D1_Mini1.D7, U1.DI
  N4: WeMos_D1_Mini1.D8, U1.RO
  N5: WeMos_D1_Mini1.G, U1.GND, J1.pin4, J2.pin1
  N6: U1.A, R1.Pin_1, J1.pin3
  N7: U1.B, R1.Pin_0, J1.pin2

notes:
  MAX3485
  5V
  GND
  R1
  A
  B
  SignalK-Modbus
  v2 2023-08
